// Logisim project processor.circ as structural Verilog: 5 circuits, main circuit main
module main (
);

  wire alu_1_zero, ALUSrc, and_1_out, Branch, Clock, Halt, Jump, JumpReg, MemRead, MemtoReg, MemWrite,
       not_1_out, RegDst, RegWrite;
  wire [1:0] ExtOp;
  wire [3:0] ALUOp, multiplexer_1_out;
  wire [12:0] register_1_q;
  wire [31:0] adder_1_out, adder_2_out, alu_1_out_4, extention_unit_1_output, multiplexer_2_out,
       multiplexer_3_out, multiplexer_4_out, multiplexer_5_out, multiplexer_6_out, multiplexer_7_out,
       ram_1_data, register_file_1_read_data_1, register_file_1_read_data_2, rom_1_data;
  wire [31:13] register_1_q_2;

  Clock clock_1 (.out(Clock));
  Register #(.width(32)) register_1 (
    .D(multiplexer_4_out), .Q({register_1_q_2, register_1_q}), .clk(Clock));  // open: en, clr
  Adder #(.width(32)) adder_1 (.a({register_1_q_2, register_1_q}), .b(32'h1), .out(adder_1_out));  // open: cin, cout
  not not_1 (not_1_out, Halt);
  ROM #(.addrWidth(13), .dataWidth(32)) rom_1 (.addr(register_1_q), .data(rom_1_data), .sel(not_1_out));
  Adder #(.width(32)) adder_2 (.a(multiplexer_5_out), .b(adder_1_out), .out(adder_2_out));  // open: cin, cout
  Control_Unit control_unit_1 (
    .in_1(rom_1_data[27:24]), .MemRead(MemRead), .MemWrite(MemWrite), .RegWrite(RegWrite), .ALUOp(ALUOp),
    .ALUSrc(ALUSrc), .MemtoReg(MemtoReg), .ExtOp(ExtOp), .RegDst(RegDst), .Branch(Branch), .Jump(Jump),
    .JumpReg(JumpReg), .Halt(Halt));
  Multiplexer #(.width(4), .disabled(0), .enable("false")) multiplexer_1 (
    .in0(rom_1_data[19:16]), .in1(rom_1_data[15:12]), .out(multiplexer_1_out), .sel(RegDst));
  Multiplexer #(.width(32), .disabled(0), .enable("false")) multiplexer_2 (
    .in0(adder_1_out), .in1(adder_2_out), .out(multiplexer_2_out), .sel(and_1_out));
  Multiplexer #(.width(32), .disabled(0), .enable("false")) multiplexer_3 (
    .in0(multiplexer_7_out), .in1(adder_1_out), .out(multiplexer_3_out), .sel(JumpReg));
  Extention_Unit extention_unit_1 (.Data(rom_1_data[15:0]), .Operation(ExtOp), .Output(extention_unit_1_output));
  Multiplexer #(.width(32), .disabled(0), .enable("false")) multiplexer_4 (
    .in0(multiplexer_2_out), .in1(multiplexer_5_out), .out(multiplexer_4_out), .sel(Jump));
  Register_File register_file_1 (
    .Read_Reg_1(rom_1_data[23:20]), .Read_Reg_2(rom_1_data[19:16]),
    .Read_Data_1(register_file_1_read_data_1), .Read_Data_2(register_file_1_read_data_2),
    .WriteEnable(RegWrite), .Write_Register(multiplexer_1_out), .Write_Data(multiplexer_3_out));
  Multiplexer #(.width(32), .disabled(0), .enable("false")) multiplexer_5 (
    .in0(extention_unit_1_output), .in1(register_file_1_read_data_1), .out(multiplexer_5_out), .sel(JumpReg));
  Multiplexer #(.width(32), .disabled(0), .enable("false")) multiplexer_6 (
    .in0(register_file_1_read_data_2), .in1(extention_unit_1_output), .out(multiplexer_6_out), .sel(ALUSrc));
  ALU alu_1 (
    .in_2(register_file_1_read_data_1), .in_3(multiplexer_6_out), .out_4(alu_1_out_4), .Operation(ALUOp),
    .Zero(alu_1_zero));
  and and_1 (and_1_out, Branch, alu_1_zero);
  RAM #(.addrWidth(13), .dataWidth(32), .bus("separate")) ram_1 (
    .addr(alu_1_out_4[12:0]), .data(ram_1_data), .str(MemWrite), .clk(Clock), .ld(MemRead));  // open: din, sel, clr
  Multiplexer #(.width(32), .disabled(0), .enable("false")) multiplexer_7 (
    .in0(alu_1_out_4), .in1(ram_1_data), .out(multiplexer_7_out), .sel(MemtoReg));
endmodule

module Register_File (
  input  WriteEnable,
  input  [3:0] Read_Reg_1,
  input  [3:0] Read_Reg_2,
  input  [31:0] Write_Data,
  input  [3:0] Write_Register,
  output [31:0] Read_Data_1,
  output [31:0] Read_Data_2
);
endmodule

module ALU (
  input  [3:0] Operation,
  input  [31:0] in_2,
  input  [31:0] in_3,
  output [31:0] out_4,
  output Zero
);
endmodule

module Extention_Unit (
  input  [1:0] Operation,
  input  [15:0] Data,
  output [31:0] Output
);
endmodule

module Control_Unit (
  input  [3:0] in_1,
  output MemRead,
  output MemWrite,
  output RegWrite,
  output [3:0] ALUOp,
  output ALUSrc,
  output MemtoReg,
  output [1:0] ExtOp,
  output RegDst,
  output Branch,
  output Jump,
  output JumpReg,
  output Halt
);


  assign Branch = 1'b0;
  assign Halt = 1'b0;
endmodule
